// Logisim project contador0_59.circ as structural Verilog: 1 circuit, main circuit main
module main (
);

  wire and_1_out, and_2_out, and_3_out, and_4_out, clk, clr, q0, q1, q2, q3, q4, q5, q6, q7, TC;

  Clock clock_1 (.out(clk));
  J_K_Flip_Flop j_k_ff_1 (.J(1'b1), .clk(clk), .K(1'b1), .Q(q0), .en(1'b1), .reset(clr));  // open: Qn, preset
  J_K_Flip_Flop j_k_ff_2 (.J(1'b1), .clk(clk), .K(1'b1), .Q(q4), .en(TC), .reset(clr));  // open: Qn, preset
  and and_1 (and_1_out, q0, q1);
  and and_2 (and_2_out, q4, q5);
  J_K_Flip_Flop j_k_ff_3 (.J(q0), .clk(clk), .K(q0), .Q(q1), .en(1'b1), .reset(clr));  // open: Qn, preset
  J_K_Flip_Flop j_k_ff_4 (.J(q4), .clk(clk), .K(q4), .Q(q5), .en(TC), .reset(clr));  // open: Qn, preset
  J_K_Flip_Flop j_k_ff_5 (.J(and_1_out), .clk(clk), .K(and_1_out), .Q(q2), .en(1'b1), .reset(clr));  // open: Qn, preset
  J_K_Flip_Flop j_k_ff_6 (.J(and_2_out), .clk(clk), .K(and_2_out), .Q(q6), .en(TC), .reset(clr));  // open: Qn, preset
  and and_3 (and_3_out, and_1_out, q2);
  and and_4 (and_4_out, and_2_out, q6);
  J_K_Flip_Flop j_k_ff_7 (.J(and_3_out), .clk(clk), .K(and_3_out), .Q(q3), .en(1'b1), .reset(clr));  // open: Qn, preset
  J_K_Flip_Flop j_k_ff_8 (.J(and_4_out), .clk(clk), .K(and_4_out), .Q(q7), .en(TC), .reset(clr));  // open: Qn, preset
  and and_5 (TC, q0, q1, q2, q3);
  and and_6 (TC, q2, q3, q4, q5);

  // Notes on the sheet:
  //   Contador 0-59
endmodule
