// Logisim project contadorbcd3.circ as structural Verilog: 1 circuit, main circuit main
module main (
);

  wire and_1_out, and_2_out, clk, clr, clr1, clr2, q0, q1, q2, q3, q4, TC;

  Clock clock_1 (.out(clk));
  J_K_Flip_Flop j_k_ff_1 (.J(1'b1), .clk(clk), .K(1'b1), .Q(q0), .en(1'b1), .reset(clr));  // open: Qn, preset
  J_K_Flip_Flop j_k_ff_2 (.J(1'b1), .clk(clk), .K(1'b1), .Q(q4), .en(TC), .reset(clr2));  // open: Qn, preset
  and and_1 (and_1_out, q0, q1);
  J_K_Flip_Flop j_k_ff_3 (.J(q0), .clk(clk), .K(q0), .Q(q1), .en(1'b1), .reset(clr));  // open: Qn, preset
  and and_2 (and_2_out, and_1_out, q2);
  J_K_Flip_Flop j_k_ff_4 (.J(and_1_out), .clk(clk), .K(and_1_out), .Q(q2), .en(1'b1), .reset(clr));  // open: Qn, preset
  J_K_Flip_Flop j_k_ff_5 (.J(and_2_out), .clk(clk), .K(and_2_out), .Q(q3), .en(1'b1), .reset(clr));  // open: Qn, preset
  and and_3 (TC, q0, q3);
  and and_4 (clr1, q1, q3);
  and and_5 (clr2, q1, q4, q0);
  or or_1 (clr, clr1, clr2);

  // Notes on the sheet:
  //   CLR 1: 10
  //   CLR : 13
endmodule
